// Logisim project Adder4bits_displays.circ as structural Verilog: 2 circuits, main circuit Adder_4bits
module Adder_4bits (
  input  A0,
  input  A1,
  input  A2,
  input  A3,
  input  B0,
  input  B1,
  input  B2,
  input  B3,
  output overflowA,
  output OVERFLOW,
  output S0,
  output S1,
  output S2,
  output S3,
  output OverflowB
);

  wire and_1_out, and_2_out, and_3_out, and_4_out, full_adder_1_vai1, full_adder_2_vai1, full_adder_3_vai1;

  Full_adder full_adder_1 (.A(A0), .B(B0), .Vem1(1'b0), .Soma(S0), .Vai1(full_adder_1_vai1));
  Full_adder full_adder_2 (.A(A1), .B(B1), .Vem1(full_adder_1_vai1), .Soma(S1), .Vai1(full_adder_2_vai1));
  and and_1 (and_1_out, A1, A3);
  and and_2 (and_2_out, B1, B3);
  or or_1 (overflowA, and_1_out, and_3_out);
  and and_3 (and_3_out, A2, A3);
  Full_adder full_adder_3 (.A(A2), .B(B2), .Vem1(full_adder_2_vai1), .Soma(S2), .Vai1(full_adder_3_vai1));
  and and_4 (and_4_out, B2, B3);
  or or_2 (OverflowB, and_2_out, and_4_out);
  Full_adder full_adder_4 (.A(A3), .B(B3), .Vem1(full_adder_3_vai1), .Soma(S3), .Vai1(OVERFLOW));
endmodule

module ripplecarry (
  input  in_1,
  input  in_2,
  input  in_3,
  input  in_4,
  input  in_5,
  input  in_6,
  input  in_7,
  input  in_8
);

  wire adder_4bits_1_overflow, adder_4bits_1_overflowa, adder_4bits_1_overflowb, adder_4bits_1_s0,
       adder_4bits_1_s1, adder_4bits_1_s2, adder_4bits_1_s3, b27seg_1_p5, b27seg_1_p6, b27seg_1_p7,
       b27seg_1_p8, b27seg_1_p9, b27seg_1_p10, b27seg_1_p11, b27seg_2_p5, b27seg_2_p6, b27seg_2_p7,
       b27seg_2_p8, b27seg_2_p9, b27seg_2_p10, b27seg_2_p11, b27seg_3_p5, b27seg_3_p6, b27seg_3_p7,
       b27seg_3_p8, b27seg_3_p9, b27seg_3_p10, b27seg_3_p11;

  // b27Seg b27seg_1: pin names not known; wires that end beside it: in_4, in_3, in_2, in_1, b27seg_1_p5, b27seg_1_p6, b27seg_1_p7, b27seg_1_p8, b27seg_1_p9, b27seg_1_p10, b27seg_1_p11
  // b27Seg b27seg_2: pin names not known; wires that end beside it: in_8, in_7, in_6, in_5, b27seg_2_p5, b27seg_2_p6, b27seg_2_p7, b27seg_2_p8, b27seg_2_p9, b27seg_2_p10, b27seg_2_p11
  _7_Segment_Display u_7_segment_display_1 (
    .b(adder_4bits_1_overflowa), .c(adder_4bits_1_overflowa));  // open: g, f, a, e, d, dp
  Adder_4bits adder_4bits_1 (
    .A0(in_1), .A1(in_2), .A2(in_3), .A3(in_4), .B0(in_5), .B1(in_6), .B2(in_7), .B3(in_8),
    .overflowA(adder_4bits_1_overflowa), .OVERFLOW(adder_4bits_1_overflow), .S0(adder_4bits_1_s0),
    .S1(adder_4bits_1_s1), .S2(adder_4bits_1_s2), .S3(adder_4bits_1_s3), .OverflowB(adder_4bits_1_overflowb));
  _7_Segment_Display u_7_segment_display_2 (
    .b(adder_4bits_1_overflowb), .c(adder_4bits_1_overflowb));  // open: g, f, a, e, d, dp
  _7_Segment_Display u_7_segment_display_3 (
    .g(b27seg_1_p11), .f(b27seg_1_p10), .a(b27seg_1_p5), .b(b27seg_1_p6), .e(b27seg_1_p9), .d(b27seg_1_p8),
    .c(b27seg_1_p7));  // open: dp
  _7_Segment_Display u_7_segment_display_4 (
    .g(b27seg_2_p11), .f(b27seg_2_p10), .a(b27seg_2_p5), .b(b27seg_2_p6), .e(b27seg_2_p9), .d(b27seg_2_p8),
    .c(b27seg_2_p7));  // open: dp
  // b27Seg b27seg_3: pin names not known; wires that end beside it: adder_4bits_1_s3, adder_4bits_1_s2, adder_4bits_1_s1, adder_4bits_1_s0, b27seg_3_p5, b27seg_3_p6, b27seg_3_p7, b27seg_3_p8, b27seg_3_p9, b27seg_3_p10, b27seg_3_p11
  _7_Segment_Display u_7_segment_display_5 (
    .b(adder_4bits_1_overflow), .c(adder_4bits_1_overflow));  // open: g, f, a, e, d, dp
  _7_Segment_Display u_7_segment_display_6 (
    .g(b27seg_3_p11), .f(b27seg_3_p10), .a(b27seg_3_p5), .b(b27seg_3_p6), .e(b27seg_3_p9), .d(b27seg_3_p8),
    .c(b27seg_3_p7));  // open: dp
endmodule
