// Logisim project Half_adder_Full_adder.circ as structural Verilog: 2 circuits, main circuit Half_adder
module Half_adder (
  input  A,
  input  B,
  output Soma,
  output Vai1
);

  and and_1 (Vai1, A, B);
  xor xor_1 (Soma, A, B);
endmodule

module Full_adder (
  input  A,
  input  B,
  input  Vem1,
  output Soma,
  output Vai1
);

  wire and_1_out, and_2_out, xor_1_out;

  xor xor_1 (xor_1_out, A, B);
  and and_1 (and_1_out, A, B);
  xor xor_2 (Soma, xor_1_out, Vem1);
  and and_2 (and_2_out, xor_1_out, Vem1);
  or or_1 (Vai1, and_2_out, and_1_out);
endmodule
